// Logisim project MyCache.circ as structural Verilog: 7 circuits, main circuit main
module main (
  input  EnableTestHalting,
  output [9:0] CorrectCounter,
  output [9:0] HitCounter,
  output [9:0] MissCounter,
  output [9:0] TestNumber,
  output [7:0] ByteRead,
  output [7:0] CorrectByteRead,
  output Halt
);

  wire and_3_out, and_4_out, and_5_out, CLK, CmdIsRead, Correct, CpuRead, CpuWrite, DidContain, HaltTesting,
       MaxItersReached, MemRead, MemWrite, not_1_out, not_2_out, not_4_out, NotDoneTesting, Ok2Count,
       or_1_out, Ready;
  wire [7:0] CpuWriteValue, MemAddress;
  wire [9:0] CpuAddress;
  wire [31:0] Line2Mem, LineFromMem;

  not not_1 (not_1_out, Ready);
  Clock clock_1 (.out(CLK));
  or or_1 (or_1_out, MaxItersReached, Ready);
  Counter #(.width(4), .max('h9)) MaxClocks (
    .load(Ready), .D(4'b0001), .count(not_1_out), .carry(MaxItersReached), .clk(CLK));  // open: Q, clr
  and and_1 (HaltTesting, EnableTestHalting, CmdIsRead, not_2_out);
  not not_2 (not_2_out, Correct);
  not not_3 (NotDoneTesting, Halt);
  Inputs inputs_1 (
    .HaltTesting(HaltTesting), .Ready(or_1_out), .CLK(CLK), .Done(Halt), .Read(CpuRead), .Write(CpuWrite),
    .Address(CpuAddress), .Value(CpuWriteValue), .TestNumber(TestNumber));
  Cache cache_1 (
    .CpuAddress(CpuAddress), .CpuRead(CpuRead), .CpuWrite(CpuWrite), .CpuWriteValue(CpuWriteValue),
    .CLK(CLK), .Ready(Ready), .DidContain(DidContain), .ByteRead(ByteRead), .MemAddress(MemAddress),
    .MemRead(MemRead), .MemWrite(MemWrite), .LineFromMem(LineFromMem), .Line2Mem(Line2Mem));
  // Probe on CpuRead
  // Probe on CpuWrite
  // Probe on CpuAddress
  // Probe on CpuWriteValue
  // Probe on TestNumber
  // Probe on CorrectByteRead
  // Probe on Correct
  // Probe on Ready
  // Probe on DidContain
  // Probe on ByteRead
  // Probe on MemAddress
  // Probe on MemRead
  // Probe on MemWrite
  // Probe on MemAddress
  // Probe on Line2Mem
  // Probe on HitCounter
  // Probe on LineFromMem
  // Probe on Line2Mem
  not not_4 (not_4_out, HaltTesting);
  RAM #(.dataWidth(32), .bus("separate")) ram_1 (
    .addr(MemAddress), .din(Line2Mem), .data(LineFromMem), .str(MemWrite), .clk(CLK), .ld(MemRead));  // open: sel, clr
  and and_2 (Ok2Count, Ready, not_4_out, NotDoneTesting);
  // Probe on LineFromMem
  and and_3 (and_3_out, Correct, Ok2Count);
  and and_4 (and_4_out, DidContain, Ok2Count);
  and and_5 (and_5_out, MemRead, NotDoneTesting);
  Checker checker_1 (
    .TestNumber(TestNumber), .YourByteRead(ByteRead), .CmdIsRead(CmdIsRead),
    .CorrectByteRead(CorrectByteRead), .Correct(Correct));
  Counter #(.width(10), .max('h3ff)) u_CorrectCounter (
    .count(and_3_out), .Q(CorrectCounter), .clk(CLK));  // open: load, D, carry, clr
  Counter #(.width(10), .max('h3ff)) u_HitCounter (
    .count(and_4_out), .Q(HitCounter), .clk(CLK));  // open: load, D, carry, clr
  Counter #(.width(10), .max('h3ff)) u_MissCounter (
    .count(and_5_out), .Q(MissCounter), .clk(CLK));  // open: load, D, carry, clr
  // Probe on CorrectCounter
  // Probe on HitCounter
  // Probe on MissCounter

  // Other names for the same wires on the sheet: DoneTesting = Halt

  // Notes on the sheet:
  //   Your Answer Inside Here
  //   Brayan Vera, 913058288
endmodule

module Cache (
  input  [9:0] CpuAddress,
  input  CpuRead,
  input  CpuWrite,
  input  [7:0] CpuWriteValue,
  input  CLK,
  input  [31:0] LineFromMem,
  output Ready,
  output DidContain,
  output [7:0] ByteRead,
  output [7:0] MemAddress,
  output MemRead,
  output MemWrite,
  output [31:0] Line2Mem
);

  wire comparator_2_eq, comparator_3_eq, comparator_4_eq, comparator_5_eq, comparator_6_gt, comparator_7_gt,
       comparator_8_gt, comparator_9_eq, comparator_10_eq, CpuRead_Saved, CpuWrite_Saved, Dirty_at__0__Saved,
       Dirty_is_set_to_0, Initialize_D__V__Age_to_0, not_1_out, Ready_Initiated, Valid_at__0__Saved,
       Valid_is_set_to_0;
  wire [1:0] Age_at__00__Saved, Age_is_set_to_00;
  wire [2:0] Counter, CpuAddress_Saved;
  wire [6:0] Cpu_Tag;
  wire [7:0] CpuWriteValue_Saved;

  Register #(.width(5)) register_1 ();  // open: D, en, Q, clk, clr
  Shift_Register #(.length(5)) Dividend ();  // open: shift, in, clk, out, load, clr, d0, q0, d1, q1, d2, q2, d3, q3, d4, q4
  Comparator #(.width(5), .mode("unsigned")) comparator_1 ();  // open: a, b, gt, eq, lt
  Multiplexer #(.width(5), .enable("false")) multiplexer_1 ();  // open: in0, in1, out, sel
  Shifter #(.width(5)) shifter_1 ();  // open: in, dist, out
  Bit_Extender #(.in_width(1), .out_width(5), .\type ("sign")) bit_extender_1 ();  // open: in, out
  Subtractor #(.width(5)) subtractor_1 ();  // open: a, b, out, bin, bout
  Counter #(.width(3), .max('h6)) Bits_Left ();  // open: load, D, count, Q, carry, clk, clr
  not not_1 (not_1_out, Initialize_D__V__Age_to_0);
  // Probe on Dirty_is_set_to_0
  // Probe on Valid_is_set_to_0
  // Probe on Age_is_set_to_00
  Counter #(.width(3), .max('h6)) Bits_Left_2 (.Q(Counter), .clk(CLK));  // open: load, D, count, carry, clr
  Comparator #(.width(1), .mode("unsigned")) comparator_2 (
    .a(CpuRead), .b(1'b0), .eq(comparator_2_eq));  // open: gt, lt
  and and_1 (Initialize_D__V__Age_to_0, comparator_2_eq, comparator_3_eq);
  Comparator #(.width(1), .mode("unsigned")) comparator_3 (
    .a(CpuWrite), .b(1'b0), .eq(comparator_3_eq));  // open: gt, lt
  not not_2 (Dirty_is_set_to_0, comparator_4_eq);
  Comparator #(.width(1), .mode("unsigned")) comparator_4 (
    .a(Initialize_D__V__Age_to_0), .b(1'b1), .eq(comparator_4_eq));  // open: gt, lt
  not not_3 (Valid_is_set_to_0, comparator_5_eq);
  Comparator #(.width(1), .mode("unsigned")) comparator_5 (
    .a(Initialize_D__V__Age_to_0), .b(1'b1), .eq(comparator_5_eq));  // open: gt, lt
  assign Age_is_set_to_00 = {{1{1'b0}}, not_1_out};  // Bit_Extender bit_extender_2
  // Probe on Age_is_set_to_00
  // Probe on Dirty_at__0__Saved
  Register #(.width(1)) Saving_initialized_Dirty (
    .D(Dirty_is_set_to_0), .en(Initialize_D__V__Age_to_0), .Q(Dirty_at__0__Saved), .clk(CLK));  // open: clr
  // Probe on Valid_at__0__Saved
  Register #(.width(1)) Saving_initialized_Valid (
    .D(Valid_is_set_to_0), .en(Initialize_D__V__Age_to_0), .Q(Valid_at__0__Saved), .clk(CLK));  // open: clr
  // Probe on Age_at__00__Saved
  Register #(.width(2)) Saving_initialized_Valid_2 (
    .D(Age_is_set_to_00), .en(Initialize_D__V__Age_to_0), .Q(Age_at__00__Saved), .clk(CLK));  // open: clr
  Comparator #(.width(1), .mode("unsigned")) comparator_6 (
    .a(Dirty_is_set_to_0), .b(Dirty_at__0__Saved), .gt(comparator_6_gt));  // open: eq, lt
  Comparator #(.width(1), .mode("unsigned")) comparator_7 (
    .a(Valid_is_set_to_0), .b(Valid_at__0__Saved), .gt(comparator_7_gt));  // open: eq, lt
  Comparator #(.width(2), .mode("unsigned")) comparator_8 (
    .a(Age_is_set_to_00), .b(Age_at__00__Saved), .gt(comparator_8_gt));  // open: eq, lt
  and and_2 (Ready_Initiated, comparator_6_gt, comparator_7_gt, comparator_8_gt);
  Comparator #(.width(3), .mode("unsigned")) comparator_9 (
    .a(Counter), .b(3'b000), .eq(comparator_9_eq));  // open: gt, lt
  Comparator #(.width(1), .mode("unsigned")) comparator_10 (
    .a(Ready_Initiated), .b(1'b1), .eq(comparator_10_eq));  // open: gt, lt
  and and_3 (Ready, comparator_9_eq, comparator_10_eq);
  // Probe on CpuAddress
  // Probe on CpuRead
  // Probe on CpuWrite
  // Probe on CpuWriteValue
  // Probe on {Cpu_Tag, CpuAddress_Saved}
  Register #(.width(10)) Saving_Address (
    .D(CpuAddress), .en(Ready), .Q({Cpu_Tag, CpuAddress_Saved}), .clk(CLK));  // open: clr
  // Probe on CpuRead_Saved
  Register #(.width(1)) Saving_CpuRead (.D(CpuRead), .en(Ready), .Q(CpuRead_Saved), .clk(CLK));  // open: clr
  // Probe on CpuWrite_Saved
  Register #(.width(1)) Saving_CPUWrite (.D(CpuWrite), .en(Ready), .Q(CpuWrite_Saved), .clk(CLK));  // open: clr
  // Probe on CpuWriteValue_Saved
  Register Saving_CpuWriteValue (.D(CpuWriteValue), .en(Ready), .Q(CpuWriteValue_Saved), .clk(CLK));  // open: clr
  // Probe on CpuAddress_Saved[1:0]
  // Probe on CpuAddress_Saved[2]
  // Probe on Cpu_Tag
  My_set My_Set_One (
    .Set(CpuAddress_Saved[2]), .CpuAddress_Saved({Cpu_Tag, CpuAddress_Saved}), .CpuRead_Saved(CpuRead_Saved),
    .CpuWrite_Saved(CpuWrite_Saved), .CpuWriteValue(CpuWriteValue_Saved),
    .Dirty_at__0__Saved(Dirty_at__0__Saved), .Valid_at__0__Saved(Valid_at__0__Saved),
    .Age_at__00__Saved(Age_at__00__Saved), .LineFromMem(LineFromMem), .Counter(Counter), .CLK(CLK),
    .Set_Contains_Tag(DidContain), .ByteRead(ByteRead), .MemAddress(MemAddress), .MemRead(MemRead),
    .MemWrite(MemWrite), .Line2Mem(Line2Mem));
  My_set My_Set_One_2 (
    .Set(CpuAddress_Saved[2]), .CpuAddress_Saved({Cpu_Tag, CpuAddress_Saved}), .CpuRead_Saved(CpuRead_Saved),
    .CpuWrite_Saved(CpuWrite_Saved), .CpuWriteValue(CpuWriteValue_Saved),
    .Dirty_at__0__Saved(Dirty_at__0__Saved), .Valid_at__0__Saved(Valid_at__0__Saved),
    .Age_at__00__Saved(Age_at__00__Saved), .LineFromMem(LineFromMem), .Counter(Counter), .CLK(CLK),
    .Set_Contains_Tag(DidContain), .ByteRead(ByteRead), .MemAddress(MemAddress), .MemRead(MemRead),
    .MemWrite(MemWrite), .Line2Mem(Line2Mem));

  // Other names for the same wires on the sheet: CpuAddress_Saved[9:3] = Cpu_Tag; Offset[1:0] = CpuAddress_Saved[1:0];
  //   Set = CpuAddress_Saved[2]

  // Notes on the sheet:
  //   Address Bits = 10
  //   Line Size = 4
  //   W = 3
  //   0000001111
  //   Num Sets = 2
  //   01011010
  //   This will indicate that my cache has TURNED ON
  //   when both write and read = 0. 
  //   After cache has turned on, we are initializing the "d,v,Dt" values
  //   We SAVE our values in new TUNNELS
  //   bc, when either ready or write is 1, will mess things up
  //   Here, Dirty_is_set_to_0 = 1 means that reading or writing
  //   has started, therefore READY has to be turned on.
  //   C =4*3*2 = 24bytes
  //   Tag bits = 7
  //   ||
  //   ||
  //   ||
  //   ||
  //   ||
  //   ||
  //   ||
  //   ||
  //   ||
  //   ||
  //   ||
  //   ||
  //   ||
  //   ||
  //   ||
  //   ||
  //   ||
  //   ||
  //   ||
  //   ||
  //   ||
  //   ||
  //   ||
  //   ||
  //   ||
  //   ||
  //   ||
  //   ||
  //   ||
  //   ||
  //   ||
  //   ||
  //   ||
  //   ||
  //   ||
  //   ||
  //   ||
  //   ||
  //   ||
  //   ||
  //   ||
  //   ||
  //   ||
  //   ||
  //   ||
  //   ||
  //   ||
  //   ||
  //   ||
  //   ||
  //   ||
  //   ||
  //   ||
  //   ||
  //   ||
  //   ||
  //   ||
  //   ||
  //   ||
  //   ||
  //   ||
  //   ||
  //   ||
  //   ||
  //   ||
  //   ||
  //   ||
  //   ||
  //   ||
  //   ||
  //   ||
  //   ||
  //   ||
  //   ||
  //   ||
  //   ||
  //   ||
  //   ||
  //   ||
  //   ||
  //   ||
  //   ||
  //   ||
  //   ||
  //   ||
  //   ||
  //   ||
  //   ||
  //   ||
  //   ||
  //   ||
  //   ||
  //   ||
  //   ||
  //   ||
  //   ||
  //   ||
  //   ||
  //   ||
  //   ||
  //   ||
  //   ||
  //   ||
  //   ||
  //   ||
  //   ||
  //   ||
  //   ||
  //   ||
  //   ||
  //   ||
  //   ||
  //   ||
  //   ||
  //   ||
  //   ||
  //   ||
  //   ||
  //   ||
  //   ||
  //   ||
  //   ||
  //   ||
  //   ||
  //   ||
  //   ||
  //   ||
  //   ||
  //   ||
  //   ||
  //   ||
  //   ||
  //   ||
  //   ||
  //   ||
  //   ||
  //   ||
  //   ||
  //   ||
  //   ||
  //   ||
  //   ||
  //   ||
  //   ||
  //   ||
  //   ||
  //   ||
  //   ||
  //   ||
  //   ||
  //   ||
  //   ||
  //   ||
  //   ||
  //   ||
  //   ||
  //   ||
  //   ||
  //   ||
  //   ||
  //   ||
  //   ||
  //   ||
  //   ||
  //   ||
  //   ||
  //   ||
  //   ||
  //   ||
  //   ||
  //   ||
  //   ||
  //   ||
  //   ||
  //   ||
  //   ||
  //   ||
  //   ||
  //   ||
  //   ||
  //   ||
  //   ||
  //   ||
  //   ||
  //   ||
  //   ||
  //   ||
  //   ||
  //   ||
  //   ||
  //   ||
  //   ||
  //   ||
  //   ||
  //   ||
  //   ||
  //   ||
  //   ||
  //   ||
  //   ||
  //   ||
  //   ||
  //   ||
  //   ||
  //   ||
  //   ||
  //   ||
  //   ||
  //   ||
  //   ||
  //   ||
  //   ||
  //   ||
  //   ||
  //   ||
  //   ||
  //   ||
  //   ||
  //   ||
  //   ||
  //   (The cache is ready to process a new request/has completed the current request.)
  //   (The value of the byte at CpuAddress when the CPU makes a read request. )
  //   When you're reading from memory, you only do this when the cache does not contain it,
  //   (1 if the cache contained the element at CpuAddress and 0 otherwise.)
  //   (The address to memory that your cache would like to read from or write to.)
  //   set equal to the addres I WANT TO READ OR WRITE TO
  //   When you WRITE to memory, you want the MemAddr to be the accessed blocks tag + the current set number
  //   And then tell the cache to write to memory
  //   so you want the MemAddr to be the CPUtag + current set.
  //   then say that you want to read from memory
  //   (1 if your cache would like to read from memory at MemAddress and 0 otherwise)
  //   (1 if your cache would like to write memory at MemAddress and 0 otherwise)
  //   (The line you requested to read from memory.)
  //   When "MemRead" is 1, then it transfers MemAdress to LineFromMem.
  //   (The line your cache would like to write to memory at MemAddress)
  //   SAVES THIS ADDRESS INTO THE MEM ADDRESS WHEN "MEMWrite" is 1
endmodule

module Inputs (
  input  HaltTesting,
  input  Ready,
  input  CLK,
  output Done,
  output Read,
  output Write,
  output [9:0] Address,
  output [7:0] Value,
  output [9:0] TestNumber
);

  wire and_1_out, not_1_out, not_2_out;

  not not_1 (not_1_out, HaltTesting);
  not not_2 (not_2_out, Done);
  Counter #(.width(10), .max('h3ff), .ongoal("stay")) u_TestNumber (
    .count(and_1_out), .Q(TestNumber), .clk(CLK));  // open: load, D, carry, clr
  and and_1 (and_1_out, not_1_out, Ready, not_2_out);
  ROM #(.addrWidth(10), .dataWidth(21)) rom_1 (
    .addr(TestNumber), .data({Done, Read, Write, Address, Value}));  // open: sel

  // Notes on the sheet:
  //   contents of rom_1 (hex, n*v repeats v):
  //   80882 83fe6 4306b 83e0e 43701 42275 8280f 80304 41bd8 84371 43f77 41d70 4250b 44733 8253d 440d8
  //   82691 440c9 83d7c 43558 446bf 83837 842c9 43e0f 4059d 41556 80166 833b0 43a89 83142 8361c 42e66
  //   43eb6 42c00 43a0e 8165c 84682 8092a 83907 41f89 817b0 40855 82056 425e8 43ff2 8039f 42bd7 82137
  //   4416b 40273 8324a 814e4 44570 41c0f 429da 82640 8069c 8099e 414d5 41004 81beb 84113 419b1 81add
  //   83f35 425ff 829cd 40250 82945 4366d 40cc2 444f8 80814 81156 8446d 42a82 42bae 82578 41135 405d0
  //   8304b 82b3a 40972 822ba 4443a 42337 82506 80bd3 80560 83552 83955 81434 43096 43da1 81aa2 80305
  //   428e6 428cc 808a2 40e80 845f0 4215d 82765 82e29 40be5 82b74 42715 417a2 41fab 8452f 81c0a 83325
  //   44624 80205 42dfc 41333 40958 81348 42736 41069 84510 44669 826dd 8067e 408e4 44680 444e8 832ad
  //   821f8 83509 82d46 81184 432cd 80b77 4005a 440e0 81ea0 43d73 42b8c 80624 41468 42699 415ed 80fc1 0
  //   100000
endmodule

module Checker (
  input  [9:0] TestNumber,
  input  [7:0] YourByteRead,
  output CmdIsRead,
  output [7:0] CorrectByteRead,
  output Correct
);

  wire comparator_1_eq;
  wire [9:0] subtractor_1_out;

  // Probe on TestNumber
  Subtractor #(.width(10)) subtractor_1 (.a(TestNumber), .b(10'h1), .out(subtractor_1_out));  // open: bin, bout
  ROM #(.addrWidth(10), .dataWidth(9)) rom_1 (
    .addr(subtractor_1_out), .data({CmdIsRead, CorrectByteRead}));  // open: sel
  Comparator #(.mode("unsigned")) comparator_1 (
    .a(YourByteRead), .b(CorrectByteRead), .eq(comparator_1_eq));  // open: gt, lt
  and and_1 (Correct, comparator_1_eq, CmdIsRead);

  // Other names for the same wires on the sheet: Test_Number[9:0] = TestNumber

  // Notes on the sheet:
  //   Read Solutions
  //   contents of rom_1 (hex, n*v repeats v):
  //   1a3 1dc 6b 125 1 75 1dc 1c3 d8 1ab 77 70 b 33 10b d8 1c3 c9 174 58 bf 153 199 f 9d 56 1bb 13b 89 16c
  //   180 66 b6 0 e 107 1bf 1d8 167 89 118 55 1a2 e8 f2 1c3 d7 142 6b 73 1ab 18c 70 f da 1c3 14c 1d8 d5 4
  //   1d8 16b b1 1f4 1f2 ff 1da 50 1da 6d c2 f8 155 1c6 1f8 82 ae 1ff 35 d0 16b 1ae 72 175 3a 37 1ff 173
  //   1d0 158 167 1d5 96 a1 1f4 1c3 e6 cc 155 80 170 5d 1e6 166 e5 1ae 15 a2 ab 170 10f 13b 24 150 fc 33
  //   58 133 36 69 170 69 1c3 14c e4 80 e8 1ab 15d 158 1fc 135 cd 1e5 5a e0 104 73 8c 14c 68 99 ed 1a6
endmodule

module My_set (
  input  Set,
  input  [9:0] CpuAddress_Saved,
  input  CpuRead_Saved,
  input  CpuWrite_Saved,
  input  [7:0] CpuWriteValue,
  input  Dirty_at__0__Saved,
  input  Valid_at__0__Saved,
  input  [1:0] Age_at__00__Saved,
  input  [31:0] LineFromMem,
  input  [2:0] Counter,
  input  CLK,
  output Set_Contains_Tag,
  output [7:0] ByteRead,
  output [7:0] MemAddress,
  output MemRead,
  output MemWrite,
  output [31:0] Line2Mem
);

  wire Age_IS_OLD_Working_On_block_1, Age_IS_OLD_Working_On_block_2, Age_IS_OLD_Working_On_block_3,
       and_1_out, and_2_out, and_3_out, and_4_out, and_5_out, and_6_out, and_8_out, and_10_out, and_11_out,
       and_12_out, and_13_out, and_14_out, and_15_out, and_16_out, and_17_out, and_18_out, and_19_out,
       and_20_out, and_21_out, and_22_out, and_23_out, and_24_out, and_25_out, and_26_out, and_27_out,
       and_28_out, and_29_out, and_30_out, and_31_out, and_32_out, comparator_2_eq, comparator_4_eq,
       comparator_5_eq, comparator_6_eq, comparator_7_eq, comparator_8_eq, comparator_9_eq, comparator_10_eq,
       comparator_12_eq, comparator_13_eq, comparator_15_eq, comparator_16_eq, comparator_17_eq,
       comparator_18_eq, comparator_19_eq, comparator_20_eq, comparator_21_eq, comparator_23_eq,
       comparator_24_eq, comparator_25_eq, comparator_27_eq, comparator_28_eq, comparator_29_eq,
       comparator_30_eq, comparator_31_eq, comparator_32_eq, comparator_34_eq, comparator_35_eq,
       comparator_36_eq, comparator_37_eq, Counter_at_1, Counter_At_2, Counter_at_3, Counter_At_4,
       Counter_At_5, Final_Updated_Dirty_Block1, Final_Updated_Dirty_Block2, Final_Updated_Dirty_Block3,
       Final_Updated_Valid_Block1, Final_Updated_Valid_Block2, Final_Updated_Valid_Block3,
       Kick_Out_OLD_Age_Enable_block_1, Kick_Out_OLD_Age_Enable_block_2, Kick_Out_OLD_Age_Enable_block_3,
       MemRead_at_3, not_1_out, not_2_out, not_3_out, not_4_out, not_5_out, not_6_out, not_7_out, or_1_out,
       or_2_out, or_4_out, or_5_out, or_6_out, or_7_out, or_8_out, or_9_out, or_10_out, or_11_out, or_12_out,
       or_13_out, or_14_out, or_15_out, or_16_out, Updated_Dirty_At_Block1, Updated_Dirty_At_Block2,
       Updated_Dirty_At_Block3, Updated_Dirty_Saved_Block1, Updated_Dirty_Saved_Block2,
       Updated_Dirty_Saved_Block3, Updated_Valid_Block1, Updated_Valid_Block2, Updated_Valid_Block3,
       Updated_Valid_Saved_Block1, Updated_Valid_Saved_Block2, Updated_Valid_Saved_Block3;
  wire [1:0] adder_1_out, adder_2_out, adder_3_out, adder_4_out, adder_5_out, Age_at__00__Saved_BLOCK1,
       Age_at__01__Saved_BLOCK2, Age_at__10__Saved_BLOCK3, Final_Updated_Age_Block1,
       Final_Updated_Age_Block2, Final_Updated_Age_Block3, multiplexer_3_out, multiplexer_4_out,
       multiplexer_5_out, multiplexer_10_out, multiplexer_11_out, multiplexer_15_out, multiplexer_16_out,
       multiplexer_19_out, multiplexer_21_out;
  wire [6:0] Blocks_Stored_Tag_block_1, Blocks_Stored_Tag_block_2, Blocks_Stored_Tag_block_3,
       Blocks_Stored_Tag_Saved_Block1, Blocks_Stored_Tag_Saved_Block2, Blocks_Stored_Tag_Saved_Block3,
       Cpu_Tag_ALREADY_in_block;
  wire [7:0] Saved_Val_00, Saved_Val_01, Saved_Val_10, Saved_Val_11, subtractor_2_out, subtractor_3_out,
       subtractor_4_out, subtractor_5_out, subtractor_6_out, subtractor_7_out, subtractor_8_out,
       subtractor_9_out, subtractor_10_out, subtractor_11_out, subtractor_12_out, subtractor_13_out,
       Value_00_Updated_Block1, Value_00_Updated_Block2, Value_00_Updated_Block3, Value_01_Updated_Block1,
       Value_01_Updated_Block2, Value_01_Updated_Block3, Value_10_Updated_Block1, Value_10_Updated_Block2,
       Value_10_Updated_Block3, Value_11_Updated_Block1, Value_11_Updated_Block2, Value_11_Updated_Block3;
  wire [31:0] Line2Mem_Block_1, Line2Mem_Block_2, Line2Mem_Block_3;

  Register #(.width(5)) register_1 ();  // open: D, en, Q, clk, clr
  Shift_Register #(.length(5)) Dividend ();  // open: shift, in, clk, out, load, clr, d0, q0, d1, q1, d2, q2, d3, q3, d4, q4
  Comparator #(.width(5), .mode("unsigned")) comparator_1 ();  // open: a, b, gt, eq, lt
  Multiplexer #(.width(5), .enable("false")) multiplexer_1 ();  // open: in0, in1, out, sel
  Shifter #(.width(5)) shifter_1 ();  // open: in, dist, out
  Bit_Extender #(.in_width(1), .out_width(5), .\type ("sign")) bit_extender_1 ();  // open: in, out
  Subtractor #(.width(5)) subtractor_1 ();  // open: a, b, out, bin, bout
  Counter #(.width(3), .max('h6)) Bits_Left ();  // open: load, D, count, Q, carry, clk, clr
  // Probe on Counter
  Comparator #(.width(1), .mode("unsigned")) comparator_2 (
    .a(Set_Contains_Tag), .b(1'b0), .eq(comparator_2_eq));  // open: gt, lt
  Comparator #(.width(3), .mode("unsigned")) comparator_3 (.a(Counter), .b(3'b001), .eq(Counter_at_1));  // open: gt, lt
  Comparator #(.width(3), .mode("unsigned")) comparator_4 (
    .a(Counter), .b(3'b001), .eq(comparator_4_eq));  // open: gt, lt
  or or_1 (or_1_out, CpuRead_Saved, CpuWrite_Saved);
  Comparator #(.width(1), .mode("unsigned")) comparator_5 (
    .a(Valid_at__0__Saved), .b(1'b0), .eq(comparator_5_eq));  // open: gt, lt
  Comparator #(.width(1), .mode("unsigned")) comparator_6 (
    .a(Valid_at__0__Saved), .b(1'b0), .eq(comparator_6_eq));  // open: gt, lt
  and and_1 (and_1_out, comparator_5_eq, comparator_6_eq, comparator_7_eq);
  Comparator #(.width(1), .mode("unsigned")) comparator_7 (
    .a(Valid_at__0__Saved), .b(1'b0), .eq(comparator_7_eq));  // open: gt, lt
  and and_2 (and_2_out, Counter_at_1, Final_Updated_Valid_Block1, comparator_8_eq);
  Comparator #(.width(7), .mode("unsigned")) comparator_8 (
    .a(CpuAddress_Saved[9:3]), .b(Blocks_Stored_Tag_Saved_Block1), .eq(comparator_8_eq));  // open: gt, lt
  and and_3 (and_3_out, Counter_at_1, Final_Updated_Valid_Block2, comparator_9_eq);
  Comparator #(.width(7), .mode("unsigned")) comparator_9 (
    .a(CpuAddress_Saved[9:3]), .b(Blocks_Stored_Tag_Saved_Block2), .eq(comparator_9_eq));  // open: gt, lt
  and and_4 (and_4_out, Counter_at_1, Final_Updated_Valid_Block2, comparator_10_eq);
  Comparator #(.width(7), .mode("unsigned")) comparator_10 (
    .a(CpuAddress_Saved[9:3]), .b(Blocks_Stored_Tag_Saved_Block3), .eq(comparator_10_eq));  // open: gt, lt
  and and_5 (and_5_out, Age_IS_OLD_Working_On_block_2, Counter_at_3, comparator_2_eq, Final_Updated_Dirty_Block2, Final_Updated_Valid_Block2);
  Multiplexer #(.width(7), .enable("false")) multiplexer_2 (
    .in0(CpuAddress_Saved[9:3]), .in1(Blocks_Stored_Tag_Saved_Block2), .out(Cpu_Tag_ALREADY_in_block),
    .sel(and_5_out));
  not not_1 (not_1_out, and_6_out);
  and and_6 (and_6_out, comparator_4_eq, or_1_out, and_1_out);
  or or_2 (or_2_out, and_2_out, and_3_out, and_4_out);
  or or_3 (Set_Contains_Tag, not_1_out, or_2_out);
  // Probe on Age_at__00__Saved_BLOCK1
  Comparator #(.width(3), .mode("unsigned")) comparator_11 (
    .a(Counter), .b(3'b101), .eq(Counter_At_5));  // open: gt, lt
  Comparator #(.width(1), .mode("unsigned")) comparator_12 (
    .a(Updated_Valid_Saved_Block1), .b(1'b1), .eq(comparator_12_eq));  // open: gt, lt
  Comparator #(.width(1), .mode("unsigned")) comparator_13 (
    .a(Age_IS_OLD_Working_On_block_1), .b(1'b1), .eq(comparator_13_eq));  // open: gt, lt
  Adder #(.width(2)) adder_1 (.a(Age_at__00__Saved_BLOCK1), .b(2'b01), .out(adder_1_out));  // open: cin, cout
  Multiplexer #(.width(2), .enable("false")) multiplexer_3 (
    .in0(adder_1_out), .in1(Age_at__00__Saved_BLOCK1), .out(multiplexer_3_out), .sel(comparator_13_eq));
  // Probe on CpuAddress_Saved[9:3]
  // Probe on CpuAddress_Saved[9:3]
  // Probe on Cpu_Tag_ALREADY_in_block
  Comparator #(.width(3), .mode("unsigned")) comparator_14 (
    .a(Counter), .b(3'b011), .eq(Counter_at_3));  // open: gt, lt
  Comparator #(.width(1), .mode("unsigned")) comparator_15 (
    .a(Dirty_at__0__Saved), .b(1'b0), .eq(comparator_15_eq));  // open: gt, lt
  Comparator #(.width(1), .mode("unsigned")) comparator_16 (
    .a(Valid_at__0__Saved), .b(1'b0), .eq(comparator_16_eq));  // open: gt, lt
  Comparator #(.width(1), .mode("unsigned")) comparator_17 (
    .a(Set_Contains_Tag), .b(1'b0), .eq(comparator_17_eq));  // open: gt, lt
  Comparator #(.width(1), .mode("unsigned")) comparator_18 (
    .a(Set_Contains_Tag), .b(1'b0), .eq(comparator_18_eq));  // open: gt, lt
  not not_2 (not_2_out, or_4_out);
  or or_4 (or_4_out, Dirty_at__0__Saved, Valid_at__0__Saved);
  Multiplexer #(.width(2), .enable("false")) multiplexer_4 (
    .in0(multiplexer_3_out), .in1(2'b00), .out(multiplexer_4_out), .sel(comparator_12_eq));
  Register #(.width(2)) register_2 (
    .D(multiplexer_5_out), .en(Counter_At_5), .Q(Age_at__00__Saved_BLOCK1), .clk(CLK));  // open: clr
  // Probe on CpuAddress_Saved[2]
  and and_7 (MemRead, Counter_at_3, comparator_15_eq, comparator_16_eq);
  Comparator #(.width(3), .mode("unsigned")) comparator_19 (
    .a(Counter), .b(3'b010), .eq(comparator_19_eq));  // open: gt, lt
  Comparator #(.width(1), .mode("unsigned")) comparator_20 (
    .a(Dirty_at__0__Saved), .b(1'b1), .eq(comparator_20_eq));  // open: gt, lt
  Comparator #(.width(1), .mode("unsigned")) comparator_21 (
    .a(Valid_at__0__Saved), .b(1'b1), .eq(comparator_21_eq));  // open: gt, lt
  // Probe on LineFromMem[7:0]
  // Probe on LineFromMem[15:8]
  // Probe on LineFromMem[23:16]
  // Probe on LineFromMem[31:24]
  or or_5 (or_5_out, CpuRead_Saved, CpuWrite_Saved);
  Comparator #(.width(3), .mode("unsigned")) comparator_22 (
    .a(Counter), .b(3'b011), .eq(Counter_at_3));  // open: gt, lt
  and and_8 (and_8_out, Age_IS_OLD_Working_On_block_3, Counter_at_3, comparator_18_eq, Final_Updated_Dirty_Block3, Final_Updated_Valid_Block3);
  Multiplexer #(.width(2), .enable("false")) multiplexer_5 (
    .in0(multiplexer_4_out), .in1(2'b00), .out(multiplexer_5_out), .sel(not_2_out));
  // Probe on CpuAddress_Saved[1:0]
  Multiplexer #(.width(8), .enable("false")) multiplexer_6 (
    .in0(CpuAddress_Saved[9:2]), .in1({Cpu_Tag_ALREADY_in_block, CpuAddress_Saved[2]}), .out(MemAddress),
    .sel(MemWrite));
  and and_9 (MemWrite, comparator_19_eq, comparator_20_eq, comparator_21_eq);
  and and_10 (and_10_out, or_5_out, MemRead);
  and and_11 (and_11_out, Age_IS_OLD_Working_On_block_1, Counter_at_3, comparator_17_eq, Final_Updated_Dirty_Block1, Final_Updated_Valid_Block1);
  Multiplexer #(.width(7), .enable("false")) multiplexer_7 (
    .in0(CpuAddress_Saved[9:3]), .in1(Blocks_Stored_Tag_Saved_Block1), .out(Cpu_Tag_ALREADY_in_block),
    .sel(and_11_out));
  Multiplexer #(.width(7), .enable("false")) multiplexer_8 (
    .in0(CpuAddress_Saved[9:3]), .in1(Blocks_Stored_Tag_Saved_Block3), .out(Cpu_Tag_ALREADY_in_block),
    .sel(and_8_out));
  // Probe on LineFromMem[7:0]
  Register register_3 (.D(LineFromMem[7:0]), .en(MemRead), .Q(Saved_Val_00), .clk(CLK));  // open: clr
  // Probe on LineFromMem[15:8]
  Register register_4 (.D(LineFromMem[15:8]), .en(MemRead), .Q(Saved_Val_01), .clk(CLK));  // open: clr
  // Probe on LineFromMem[23:16]
  Register register_5 (.D(LineFromMem[23:16]), .en(MemRead), .Q(Saved_Val_10), .clk(CLK));  // open: clr
  // Probe on LineFromMem[31:24]
  Register register_6 (.D(LineFromMem[31:24]), .en(MemRead), .Q(Saved_Val_11), .clk(CLK));  // open: clr
  Multiplexer #(.width(8), .enable("false")) multiplexer_9 (
    .in0({8{1'b0}}), .in1(CpuAddress_Saved[9:2]), .out(ByteRead), .sel(and_10_out));
  Register #(.width(1)) register_7 (.D(MemRead), .en(Counter_at_3), .Q(MemRead_at_3), .clk(CLK));  // open: clr
  // Probe on Saved_Val_00
  // Probe on Saved_Val_01
  // Probe on Saved_Val_10
  // Probe on Saved_Val_11
  // Probe on Age_at__01__Saved_BLOCK2
  Comparator #(.width(1), .mode("unsigned")) comparator_23 (
    .a(Age_IS_OLD_Working_On_block_2), .b(1'b1), .eq(comparator_23_eq));  // open: gt, lt
  Adder #(.width(2)) adder_2 (.a(Age_at__01__Saved_BLOCK2), .b(2'b01), .out(adder_2_out));  // open: cin, cout
  Comparator #(.width(1), .mode("unsigned")) comparator_24 (
    .a(MemRead_at_3), .b(1'b1), .eq(comparator_24_eq));  // open: gt, lt
  Comparator #(.width(1), .mode("unsigned")) comparator_25 (
    .a(Updated_Valid_Saved_Block2), .b(1'b1), .eq(comparator_25_eq));  // open: gt, lt
  Multiplexer #(.width(2), .enable("false")) multiplexer_10 (
    .in0(adder_2_out), .in1(Age_at__01__Saved_BLOCK2), .out(multiplexer_10_out), .sel(comparator_23_eq));
  // Probe on Age_at__00__Saved
  Adder #(.width(2)) adder_3 (.a(Age_at__00__Saved), .b(2'b01), .out(adder_3_out));  // open: cin, cout
  // Probe on adder_3_out
  Adder #(.width(2)) adder_4 (.a(Age_at__00__Saved), .b(2'b10), .out(adder_4_out));  // open: cin, cout
  // Probe on adder_4_out
  Comparator #(.width(3), .mode("unsigned")) comparator_26 (
    .a(Counter), .b(3'b100), .eq(Counter_At_4));  // open: gt, lt
  or or_6 (or_6_out, Set, Kick_Out_OLD_Age_Enable_block_1);
  and and_12 (and_12_out, Counter_At_4, comparator_27_eq);
  Comparator #(.width(1), .mode("unsigned")) comparator_27 (
    .a(MemRead_at_3), .b(1'b1), .eq(comparator_27_eq));  // open: gt, lt
  or or_7 (or_7_out, Set, Kick_Out_OLD_Age_Enable_block_2);
  and and_13 (and_13_out, Counter_At_4, comparator_28_eq);
  Comparator #(.width(1), .mode("unsigned")) comparator_28 (
    .a(MemRead_at_3), .b(1'b1), .eq(comparator_28_eq));  // open: gt, lt
  Register #(.width(1)) register_8 (
    .D(Updated_Dirty_At_Block2), .en(Counter_At_4), .Q(Updated_Dirty_Saved_Block2), .clk(CLK));  // open: clr
  or or_8 (or_8_out, Set, Kick_Out_OLD_Age_Enable_block_3);
  and and_14 (and_14_out, Counter_At_4, comparator_24_eq);
  Register #(.width(1)) register_9 (
    .D(Updated_Dirty_At_Block3), .en(Counter_At_4), .Q(Updated_Dirty_Saved_Block3), .clk(CLK));  // open: clr
  or or_9 (or_9_out, Dirty_at__0__Saved, Valid_at__0__Saved);
  not not_3 (not_3_out, or_9_out);
  Multiplexer #(.width(2), .enable("false")) multiplexer_11 (
    .in0(multiplexer_10_out), .in1(2'b00), .out(multiplexer_11_out), .sel(comparator_25_eq));
  Register #(.width(2)) register_10 (
    .D(multiplexer_15_out), .en(Counter_At_5), .Q(Age_at__01__Saved_BLOCK2), .clk(CLK));  // open: clr
  and and_15 (and_15_out, or_6_out, and_12_out);
  Multiplexer #(.enable("false")) multiplexer_12 (
    .in0(Dirty_at__0__Saved), .in1(Dirty_at__0__Saved), .out(Updated_Dirty_At_Block1), .sel(and_15_out));
  Register #(.width(1)) register_11 (
    .D(Updated_Dirty_At_Block1), .en(Counter_At_4), .Q(Updated_Dirty_Saved_Block1), .clk(CLK));  // open: clr
  and and_16 (and_16_out, or_7_out, and_13_out);
  Multiplexer #(.enable("false")) multiplexer_13 (
    .in0(Dirty_at__0__Saved), .in1(Dirty_at__0__Saved), .out(Updated_Dirty_At_Block2), .sel(and_16_out));
  and and_17 (and_17_out, or_8_out, and_14_out);
  Multiplexer #(.enable("false")) multiplexer_14 (
    .in0(Dirty_at__0__Saved), .in1(Dirty_at__0__Saved), .out(Updated_Dirty_At_Block3), .sel(and_17_out));
  Multiplexer #(.width(2), .enable("false")) multiplexer_15 (
    .in0(multiplexer_11_out), .in1(2'b01), .out(multiplexer_15_out), .sel(not_3_out));
  Kick_Out_the_Oldest_Age_Only Kick_out_at_this_Block (
    .Contain(Set_Contains_Tag), .Counter(Counter), .Age_at__00__Saved(Age_at__00__Saved_BLOCK1),
    .Age_at__01__Saved(Age_at__01__Saved_BLOCK2), .Age_at__10__Saved(Age_at__10__Saved_BLOCK3),
    .Kick_Out_Age_In_Block_1(Kick_Out_OLD_Age_Enable_block_1),
    .Kick_Out_Age_In_Block_2(Kick_Out_OLD_Age_Enable_block_2),
    .Kick_Out_Age_In_Block_3(Kick_Out_OLD_Age_Enable_block_3));
  and and_18 (and_18_out, Counter_At_4, comparator_29_eq);
  Comparator #(.width(1), .mode("unsigned")) comparator_29 (
    .a(MemRead_at_3), .b(1'b1), .eq(comparator_29_eq));  // open: gt, lt
  and and_19 (and_19_out, Counter_At_4, comparator_30_eq);
  Comparator #(.width(1), .mode("unsigned")) comparator_30 (
    .a(MemRead_at_3), .b(1'b1), .eq(comparator_30_eq));  // open: gt, lt
  Comparator #(.width(1), .mode("unsigned")) comparator_31 (
    .a(MemRead_at_3), .b(1'b1), .eq(comparator_31_eq));  // open: gt, lt
  Comparator #(.width(1), .mode("unsigned")) comparator_32 (
    .a(Age_IS_OLD_Working_On_block_3), .b(1'b1), .eq(comparator_32_eq));  // open: gt, lt
  Adder #(.width(2)) adder_5 (.a(Age_at__10__Saved_BLOCK3), .b(2'b01), .out(adder_5_out));  // open: cin, cout
  Multiplexer #(.width(2), .enable("false")) multiplexer_16 (
    .in0(adder_5_out), .in1(Age_at__10__Saved_BLOCK3), .out(multiplexer_16_out), .sel(comparator_32_eq));
  Comparator #(.width(3), .mode("unsigned")) comparator_33 (
    .a(Counter), .b(3'b010), .eq(Counter_At_2));  // open: gt, lt
  Register #(.width(1)) register_12 (
    .D(Kick_Out_OLD_Age_Enable_block_1), .en(Counter_At_2), .Q(Age_IS_OLD_Working_On_block_1), .clk(CLK));  // open: clr
  Register #(.width(1)) register_13 (
    .D(Kick_Out_OLD_Age_Enable_block_2), .en(Counter_At_2), .Q(Age_IS_OLD_Working_On_block_2), .clk(CLK));  // open: clr
  Register #(.width(1)) register_14 (
    .D(Kick_Out_OLD_Age_Enable_block_3), .en(Counter_At_2), .Q(Age_IS_OLD_Working_On_block_3), .clk(CLK));  // open: clr
  or or_10 (or_10_out, Set, Kick_Out_OLD_Age_Enable_block_1);
  Multiplexer #(.enable("false")) multiplexer_17 (
    .in0(Valid_at__0__Saved), .in1(not_4_out), .out(Updated_Valid_Block1), .sel(and_21_out));
  not not_4 (not_4_out, Valid_at__0__Saved);
  Register #(.width(1)) register_15 (
    .D(Updated_Valid_Block1), .en(Counter_At_4), .Q(Updated_Valid_Saved_Block1), .clk(CLK));  // open: clr
  or or_11 (or_11_out, Set, Kick_Out_OLD_Age_Enable_block_2);
  Multiplexer #(.enable("false")) multiplexer_18 (
    .in0(Valid_at__0__Saved), .in1(not_5_out), .out(Updated_Valid_Block2), .sel(and_22_out));
  not not_5 (not_5_out, Valid_at__0__Saved);
  Register #(.width(1)) register_16 (
    .D(Updated_Valid_Block2), .en(Counter_At_4), .Q(Updated_Valid_Saved_Block2), .clk(CLK));  // open: clr
  or or_12 (or_12_out, Set, Kick_Out_OLD_Age_Enable_block_3);
  and and_20 (and_20_out, Counter_At_4, comparator_31_eq);
  not not_6 (not_6_out, Valid_at__0__Saved);
  Register #(.width(1)) register_17 (
    .D(Updated_Valid_Block3), .en(Counter_At_4), .Q(Updated_Valid_Saved_Block3), .clk(CLK));  // open: clr
  not not_7 (not_7_out, or_13_out);
  or or_13 (or_13_out, Dirty_at__0__Saved, Valid_at__0__Saved);
  Comparator #(.width(1), .mode("unsigned")) comparator_34 (
    .a(Updated_Valid_Saved_Block3), .b(1'b1), .eq(comparator_34_eq));  // open: gt, lt
  Multiplexer #(.width(2), .enable("false")) multiplexer_19 (
    .in0(multiplexer_16_out), .in1(2'b00), .out(multiplexer_19_out), .sel(comparator_34_eq));
  Register #(.width(2)) register_18 (
    .D(multiplexer_21_out), .en(Counter_At_5), .Q(Age_at__10__Saved_BLOCK3), .clk(CLK));  // open: clr
  and and_21 (and_21_out, or_10_out, and_18_out);
  and and_22 (and_22_out, or_11_out, and_19_out);
  and and_23 (and_23_out, or_12_out, and_20_out);
  Multiplexer #(.enable("false")) multiplexer_20 (
    .in0(Valid_at__0__Saved), .in1(not_6_out), .out(Updated_Valid_Block3), .sel(and_23_out));
  Multiplexer #(.width(2), .enable("false")) multiplexer_21 (
    .in0(multiplexer_19_out), .in1(2'b10), .out(multiplexer_21_out), .sel(not_7_out));
  Comparator #(.width(1), .mode("unsigned")) comparator_35 (
    .a(MemRead_at_3), .b(1'b1), .eq(comparator_35_eq));  // open: gt, lt
  // Probe on Blocks_Stored_Tag_block_1
  Comparator #(.width(1), .mode("unsigned")) comparator_36 (
    .a(MemRead_at_3), .b(1'b1), .eq(comparator_36_eq));  // open: gt, lt
  // Probe on Blocks_Stored_Tag_block_2
  Comparator #(.width(1), .mode("unsigned")) comparator_37 (
    .a(MemRead_at_3), .b(1'b1), .eq(comparator_37_eq));  // open: gt, lt
  // Probe on Blocks_Stored_Tag_block_3
  or or_14 (or_14_out, Set, Kick_Out_OLD_Age_Enable_block_1);
  and and_24 (and_24_out, Counter_At_4, comparator_35_eq);
  // Probe on Blocks_Stored_Tag_Saved_Block1
  Register #(.width(7)) register_19 (
    .D(Blocks_Stored_Tag_block_1), .en(Counter_At_4), .Q(Blocks_Stored_Tag_Saved_Block1), .clk(CLK));  // open: clr
  or or_15 (or_15_out, Set, Kick_Out_OLD_Age_Enable_block_2);
  and and_25 (and_25_out, Counter_At_4, comparator_36_eq);
  // Probe on Blocks_Stored_Tag_Saved_Block2
  Register #(.width(7)) register_20 (
    .D(Blocks_Stored_Tag_block_2), .en(Counter_At_4), .Q(Blocks_Stored_Tag_Saved_Block2), .clk(CLK));  // open: clr
  or or_16 (or_16_out, Set, Kick_Out_OLD_Age_Enable_block_3);
  and and_26 (and_26_out, Counter_At_4, comparator_37_eq);
  // Probe on Blocks_Stored_Tag_Saved_Block3
  Register #(.width(7)) register_21 (
    .D(Blocks_Stored_Tag_block_3), .en(Counter_At_4), .Q(Blocks_Stored_Tag_Saved_Block3), .clk(CLK));  // open: clr
  My_Block my_block_1 (
    .Set(Age_IS_OLD_Working_On_block_1), .CpuAddress_Saved(Blocks_Stored_Tag_Saved_Block1),
    .Dirty(Updated_Dirty_Saved_Block1), .Valid(Updated_Valid_Saved_Block1), .Age(Age_at__00__Saved_BLOCK1),
    .Value_00(LineFromMem[7:0]), .Value_01(LineFromMem[15:8]), .Value_10(LineFromMem[23:16]),
    .Value_11(LineFromMem[31:24]), .CLK(CLK), .Final_TAG(Blocks_Stored_Tag_Saved_Block1),
    .Updated_Dirty(Final_Updated_Dirty_Block1), .Updated_Valid(Final_Updated_Valid_Block1),
    .Updated_Age(Final_Updated_Age_Block1), .Value_00_Updated(Value_00_Updated_Block1),
    .Value_01_Updated(Value_01_Updated_Block1), .Value_10_Updated(Value_10_Updated_Block1),
    .Value_11_Updated(Value_11_Updated_Block1));
  My_Block my_block_2 (
    .Set(Age_IS_OLD_Working_On_block_2), .CpuAddress_Saved(Blocks_Stored_Tag_Saved_Block2),
    .Dirty(Updated_Dirty_Saved_Block2), .Valid(Updated_Valid_Saved_Block1), .Age(Age_at__01__Saved_BLOCK2),
    .Value_00(LineFromMem[7:0]), .Value_01(LineFromMem[15:8]), .Value_10(LineFromMem[23:16]),
    .Value_11(LineFromMem[31:24]), .CLK(CLK), .Final_TAG(Blocks_Stored_Tag_Saved_Block2),
    .Updated_Dirty(Final_Updated_Dirty_Block2), .Updated_Valid(Final_Updated_Valid_Block2),
    .Updated_Age(Final_Updated_Age_Block2), .Value_00_Updated(Value_00_Updated_Block2),
    .Value_01_Updated(Value_01_Updated_Block2), .Value_10_Updated(Value_10_Updated_Block2),
    .Value_11_Updated(Value_11_Updated_Block2));
  My_Block my_block_3 (
    .Set(Age_IS_OLD_Working_On_block_3), .CpuAddress_Saved(Blocks_Stored_Tag_Saved_Block3),
    .Dirty(Updated_Dirty_Saved_Block3), .Valid(Updated_Valid_Saved_Block3), .Age(Age_at__10__Saved_BLOCK3),
    .Value_00(LineFromMem[7:0]), .Value_01(LineFromMem[15:8]), .Value_10(LineFromMem[23:16]),
    .Value_11(LineFromMem[31:24]), .CLK(CLK), .Final_TAG(Blocks_Stored_Tag_Saved_Block3),
    .Updated_Dirty(Final_Updated_Dirty_Block3), .Updated_Valid(Final_Updated_Valid_Block3),
    .Updated_Age(Final_Updated_Age_Block3), .Value_00_Updated(Value_00_Updated_Block3),
    .Value_01_Updated(Value_01_Updated_Block3), .Value_10_Updated(Value_10_Updated_Block3),
    .Value_11_Updated(Value_11_Updated_Block3));
  and and_27 (and_27_out, Final_Updated_Valid_Block1, or_14_out, and_24_out);
  Multiplexer #(.width(7), .enable("false")) multiplexer_22 (
    .in0({7{1'b0}}), .in1(CpuAddress_Saved[9:3]), .out(Blocks_Stored_Tag_block_1), .sel(and_27_out));
  and and_28 (and_28_out, Final_Updated_Valid_Block2, or_15_out, and_25_out);
  Multiplexer #(.width(7), .enable("false")) multiplexer_23 (
    .in0({7{1'b0}}), .in1(CpuAddress_Saved[9:3]), .out(Blocks_Stored_Tag_block_2), .sel(and_28_out));
  and and_29 (and_29_out, Final_Updated_Valid_Block3, or_16_out, and_26_out);
  Multiplexer #(.width(7), .enable("false")) multiplexer_24 (
    .in0({7{1'b0}}), .in1(CpuAddress_Saved[9:3]), .out(Blocks_Stored_Tag_block_3), .sel(and_29_out));
  Subtractor subtractor_2 (
    .a(Value_00_Updated_Block2), .b(Value_00_Updated_Block2), .out(subtractor_2_out));  // open: bin, bout
  Subtractor subtractor_3 (
    .a(Value_01_Updated_Block2), .b(Value_01_Updated_Block2), .out(subtractor_3_out));  // open: bin, bout
  Subtractor subtractor_4 (
    .a(Value_10_Updated_Block2), .b(Value_10_Updated_Block2), .out(subtractor_4_out));  // open: bin, bout
  Subtractor subtractor_5 (
    .a(Value_11_Updated_Block2), .b(Value_11_Updated_Block2), .out(subtractor_5_out));  // open: bin, bout
  Subtractor subtractor_6 (
    .a(Value_00_Updated_Block3), .b(Value_00_Updated_Block1), .out(subtractor_6_out));  // open: bin, bout
  Subtractor subtractor_7 (
    .a(Value_01_Updated_Block3), .b(Value_01_Updated_Block1), .out(subtractor_7_out));  // open: bin, bout
  Subtractor subtractor_8 (
    .a(Value_10_Updated_Block3), .b(Value_10_Updated_Block3), .out(subtractor_8_out));  // open: bin, bout
  Subtractor subtractor_9 (
    .a(Value_11_Updated_Block3), .b(Value_11_Updated_Block3), .out(subtractor_9_out));  // open: bin, bout
  Subtractor subtractor_10 (
    .a(Value_00_Updated_Block1), .b(Value_00_Updated_Block1), .out(subtractor_10_out));  // open: bin, bout
  Subtractor subtractor_11 (
    .a(Value_01_Updated_Block1), .b(Value_01_Updated_Block1), .out(subtractor_11_out));  // open: bin, bout
  Subtractor subtractor_12 (
    .a(Value_10_Updated_Block1), .b(Value_10_Updated_Block1), .out(subtractor_12_out));  // open: bin, bout
  Subtractor subtractor_13 (
    .a(Value_11_Updated_Block1), .b(Value_11_Updated_Block1), .out(subtractor_13_out));  // open: bin, bout
  and and_30 (and_30_out, MemWrite, Age_IS_OLD_Working_On_block_1);
  and and_31 (and_31_out, MemWrite, Age_IS_OLD_Working_On_block_1);
  and and_32 (and_32_out, MemWrite, Age_IS_OLD_Working_On_block_1);
  Adder adder_6 (.a(subtractor_2_out), .b(MemAddress), .out(Line2Mem_Block_1[7:0]));  // open: cin, cout
  Adder adder_7 (.a(subtractor_3_out), .b(MemAddress), .out(Line2Mem_Block_1[15:8]));  // open: cin, cout
  Adder adder_8 (.a(subtractor_4_out), .b(MemAddress), .out(Line2Mem_Block_1[23:16]));  // open: cin, cout
  Adder adder_9 (.a(subtractor_5_out), .b(MemAddress), .out(Line2Mem_Block_1[31:24]));  // open: cin, cout
  Adder adder_10 (.a(subtractor_6_out), .b(MemAddress), .out(Line2Mem_Block_2[7:0]));  // open: cin, cout
  Adder adder_11 (.a(subtractor_7_out), .b(MemAddress), .out(Line2Mem_Block_2[15:8]));  // open: cin, cout
  Adder adder_12 (.a(subtractor_8_out), .b(MemAddress), .out(Line2Mem_Block_2[23:16]));  // open: cin, cout
  Adder adder_13 (.a(subtractor_9_out), .b(MemAddress), .out(Line2Mem_Block_2[31:24]));  // open: cin, cout
  Adder adder_14 (.a(subtractor_10_out), .b(MemAddress), .out(Line2Mem_Block_3[7:0]));  // open: cin, cout
  Adder adder_15 (.a(subtractor_11_out), .b(MemAddress), .out(Line2Mem_Block_3[15:8]));  // open: cin, cout
  Adder adder_16 (.a(subtractor_12_out), .b(MemAddress), .out(Line2Mem_Block_3[23:16]));  // open: cin, cout
  Adder adder_17 (.a(subtractor_13_out), .b(MemAddress), .out(Line2Mem_Block_3[31:24]));  // open: cin, cout
  Multiplexer #(.width(32), .enable("false")) multiplexer_25 (
    .in0(LineFromMem), .in1(Line2Mem_Block_1), .out(Line2Mem), .sel(and_30_out));
  Multiplexer #(.width(32), .enable("false")) multiplexer_26 (
    .in0(LineFromMem), .in1(Line2Mem_Block_2), .out(Line2Mem), .sel(and_31_out));
  Multiplexer #(.width(32), .enable("false")) multiplexer_27 (
    .in0(LineFromMem), .in1(Line2Mem_Block_3), .out(Line2Mem), .sel(and_32_out));

  // Other names for the same wires on the sheet: Set_t = CpuAddress_Saved[2]; Cpu_Tag[6:0] = CpuAddress_Saved[9:3];
  //   Try_TAG[6:0] = CpuAddress_Saved[9:3]; Contains = Set_Contains_Tag;
  //   Dirty_at__0__Saved_BLOCK1 = Dirty_at__0__Saved; Dirty_at__0__Saved_BLOCK2 = Dirty_at__0__Saved;
  //   Dirty_at__0__Saved_BLOCK3 = Dirty_at__0__Saved; NewVal_00_block_2[7:0] = Line2Mem_Block_1[7:0];
  //   NewVal_01_block_2[7:0] = Line2Mem_Block_1[15:8]; NewVal_10_block_2[7:0] = Line2Mem_Block_1[23:16];
  //   NewVal_11_block_2[7:0] = Line2Mem_Block_1[31:24]; NewVal_00_block_3[7:0] = Line2Mem_Block_2[7:0];
  //   NewVal_01_block_3[7:0] = Line2Mem_Block_2[15:8]; NewVal_10_block_3[7:0] = Line2Mem_Block_2[23:16];
  //   NewVal_11_block_3[7:0] = Line2Mem_Block_2[31:24]; NewVal_00_block_1[7:0] = Line2Mem_Block_3[7:0];
  //   NewVal_01_block_1[7:0] = Line2Mem_Block_3[15:8]; NewVal_10_block_1[7:0] = Line2Mem_Block_3[23:16];
  //   NewVal_11_block_1[7:0] = Line2Mem_Block_3[31:24]; Val_00[7:0] = LineFromMem[7:0];
  //   Val_01[7:0] = LineFromMem[15:8]; Offset[1:0] = CpuAddress_Saved[1:0]; Set_In_This_Block_Is_On = Set;
  //   Val_10[7:0] = LineFromMem[23:16]; Val_11[7:0] = LineFromMem[31:24];
  //   Valid_at__0__Saved_BLOCK1 = Valid_at__0__Saved; Valid_at__0__Saved_BLOCK2 = Valid_at__0__Saved;
  //   Valid_at__0__Saved_BLOCK3 = Valid_at__0__Saved

  // Notes on the sheet:
  //   does not contain
  //   Initializing Ages in each block
  //   The Line you requested to read from memory
  //   2
  //   0000001111
  //   One case for contains:
  //   Means that we have started to read or write
  //   and all the valids in the set are "0" to start with
  //   therefore, it means that it does not contain a matching TAG
  //   The Other Case is for when the valid is "1" and then
  //   when looking for the Tag inside the block, it turns out that there
  //   is a matching Tag. This means that this set DOES CONTAIN a matching Tag.
  //   01011010
  //   ||
  //   ||
  //   ||
  //   ||
  //   ||
  //   ||
  //   ||
  //   ||
  //   ||
  //   ||
  //   ||
  //   ||
  //   ||
  //   ||
  //   ||
  //   ||
  //   ||
  //   ||
  //   ||
  //   ||
  //   ||
  //   ||
  //   ||
  //   ||
  //   ||
  //   ||
  //   ||
  //   ||
  //   ||
  //   ||
  //   ||
  //   ||
  //   ||
  //   ||
  //   ||
  //   ||
  //   ||
  //   ||
  //   ||
  //   ||
  //   ||
  //   ||
  //   ||
  //   ||
  //   ||
  //   ||
  //   ||
  //   ||
  //   ||
  //   ||
  //   ||
  //   ||
  //   ||
  //   ||
  //   ||
  //   ||
  //   ||
  //   ||
  //   ||
  //   ||
  //   ||
  //   ||
  //   ||
  //   ||
  //   ||
  //   ||
  //   ||
  //   ||
  //   ||
  //   ||
  //   ||
  //   ||
  //   ||
  //   ||
  //   ||
  //   ||
  //   ||
  //   ||
  //   ||
  //   ||
  //   ||
  //   ||
  //   ||
  //   ||
  //   ||
  //   ||
  //   ||
  //   ||
  //   ||
  //   ||
  //   ||
  //   ||
  //   ||
  //   ||
  //   ||
  //   ||
  //   ||
  //   ||
  //   ||
  //   ||
  //   ||
  //   does not contain
  //   does not contain
  //   Updating Age Process
  //   This is the real thing that we have to do
  //   I think the Values are already inside the Block
  //   ???????I don't know If I need to save these values. Maybe not
  //   I think I need to save them when read is enabled
  //   The MemAdress in the Main circuit will go to the RAM and give me my LineFromMem
  //   Doing ByteRead when Ready (also meaninf write or read has initiated and Memread is 1)
  //   I will make MemRead also dependent on the counter
  //   But, maybe I should just make it dependent on Valid and Dirty to be both 0
  //   But, I'm doing both anyways
  //   <--------------------
  //   ||
  //   ||
  //   ||
  //   ||
  //   ||
  //   ||
  //   ||
  //   ||
  //   ||
  //   ||
  //   ||
  //   ||
  //   ||
  //   ||
  //   ||
  //   ||
  //   ||
  //   ||
  //   ||
  //   ||
  //   ||
  //   ||
  //   ||
  //   ||
  //   ||
  //   ||
  //   ||
  //   ||
  //   ||
  //   ||
  //   ||
  //   ||
  //   ||
  //   ||
  //   ||
  //   ||
  //   ||
  //   ||
  //   ||
  //   ||
  //   ||
  //   ||
  //   ||
  //   ||
  //   ||
  //   ||
  //   ||
  //   ||
  //   ||
  //   ||
  //   ||
  //   ||
  //   ||
  //   ||
  //   ||
  //   ||
  //   ||
  //   ||
  //   ||
  //   ||
  //   ||
  //   ||
  //   ||
  //   ||
  //   ||
  //   ||
  //   ||
  //   ||
  //   ||
  //   ||
  //   ||
  //   ||
  //   ||
  //   ||
  //   ||
  //   ||
  //   ||
  //   ||
  //   ||
  //   ||
  //   ||
  //   ||
  //   ||
  //   ||
  //   ||
  //   ||
  //   ||
  //   ||
  //   ||
  //   ||
  //   ||
  //   ||
  //   ||
  //   ||
  //   ||
  //   ||
  //   ||
  //   ||
  //   ||
  //   ||
  //   ||
  //   ||
  //   ||
  //   ||
  //   ||
  //   ||
  //   ||
  //   ||
  //   ||
  //   ||
  //   ||
  //   ||
  //   ||
  //   ||
  //   ||
  //   ||
  //   ||
  //   ||
  //   ||
  //   ||
  //   ||
  //   ||
  //   ||
  //   ||
  //   ||
  //   ||
  //   ||
  //   ||
  //   ||
  //   ||
  //   ||
  //   ||
  //   ||
  //   ||
  //   ||
  //   ||
  //   ||
  //   ||
  //   ||
  //   ||
  //   ||
  //   ||
  //   ||
  //   ||
  //   ||
  //   ||
  //   ||
  //   ||
  //   ||
  //   ||
  //   ||
  //   ||
  //   ||
  //   ||
  //   ||
  //   ||
  //   ||
  //   ||
  //   ||
  //   ||
  //   ||
  //   ||
  //   ||
  //   Setting up age like this does not work
  //   DirtyBit_Remeains 0 when Read From Mem
  //   DirtyBit_Remeains 0 when Read From Mem
  //   DirtyBit_Remeains 0 when Read From Mem
  //   ===============================================
  //   Comparing MemRead to "0" because it means that we have
  //   read from memory. Therefore updates values
  //   =====================================================
  //   ||
  //   ||
  //   ||
  //   ||
  //   ||
  //   ||
  //   ||
  //   ||
  //   ||
  //   ||
  //   ||
  //   ||
  //   ||
  //   ||
  //   ||
  //   ||
  //   ||
  //   ||
  //   ||
  //   ||
  //   ||
  //   ||
  //   ||
  //   ||
  //   ||
  //   ||
  //   ||
  //   ||
  //   ||
  //   ||
  //   ||
  //   ||
  //   ||
  //   ||
  //   ||
  //   ||
  //   ||
  //   ||
  //   ||
  //   ||
  //   ||
  //   ||
  //   ||
  //   ||
  //   ||
  //   ||
  //   ||
  //   ||
  //   ||
  //   ||
  //   ||
  //   ||
  //   ||
  //   ||
  //   ||
  //   ||
  //   ||
  //   ||
  //   ||
  //   ||
  //   ||
  //   ||
  //   ||
  //   ||
  //   ||
  //   ||
  //   ||
  //   ||
  //   ||
  //   ||
  //   ||
  //   ||
  //   ||
  //   ||
  //   ||
  //   ||
  //   ||
  //   ||
  //   ||
  //   ||
  //   ||
  //   ||
  //   ||
  //   ||
  //   ||
  //   ||
  //   ||
  //   ||
  //   ||
  //   ||
  //   ||
  //   ||
  //   ||
  //   ||
  //   ||
  //   ||
  //   ||
  //   ||
  //   ||
  //   ||
  //   ||
  //   ||
  //   ||
  //   ||
  //   ||
  //   ||
  //   ||
  //   ||
  //   ||
  //   ||
  //   ||
  //   ||
  //   ||
  //   ||
  //   ||
  //   ||
  //   ||
  //   ||
  //   ||
  //   ||
  //   ||
  //   ||
  //   ||
  //   ||
  //   ||
  //   ||
  //   ||
  //   ||
  //   ||
  //   ||
  //   ||
  //   ||
  //   ||
  //   ||
  //   ||
  //   ||
  //   ||
  //   ||
  //   ||
  //   ||
  //   ||
  //   ||
  //   ||
  //   ||
  //   ||
  //   ||
  //   ||
  //   ||
  //   ||
  //   ||
  //   ||
  //   ||
  //   ||
  //   ||
  //   ||
  //   ||
  //   ||
  //   ||
  //   ||
  //   ||
  //   ||
  //   ||
  //   ||
  //   ||
  //   ||
  //   Updating VALID. when Valid is 0 = IsINVALID
  //   =====================================================
  //   when Valid is 1 = isVALID
  //   =====================================================
  //   ||
  //   ||
  //   ||
  //   ||
  //   ||
  //   ||
  //   ||
  //   ||
  //   ||
  //   ||
  //   ||
  //   ||
  //   ||
  //   ||
  //   ||
  //   ||
  //   ||
  //   ||
  //   ||
  //   ||
  //   ||
  //   ||
  //   ||
  //   ||
  //   ||
  //   ||
  //   ||
  //   ||
  //   ||
  //   ||
  //   ||
  //   ||
  //   ||
  //   ||
  //   ||
  //   ||
  //   ||
  //   ||
  //   ||
  //   ||
  //   ||
  //   ||
  //   ||
  //   ||
  //   ||
  //   ||
  //   ||
  //   ||
  //   ||
  //   ||
  //   ||
  //   ||
  //   ||
  //   ||
  //   ||
  //   ||
  //   ||
  //   ||
  //   ||
  //   ||
  //   ||
  //   ||
  //   ||
  //   ||
  //   ||
  //   ||
  //   ||
  //   ||
  //   ||
  //   ||
  //   ||
  //   ||
  //   ||
  //   ||
  //   ||
  //   ||
  //   ||
  //   ||
  //   ||
  //   ||
  //   ||
  //   ||
  //   ||
  //   ||
  //   ||
  //   ||
  //   ||
  //   ||
  //   ||
  //   ||
  //   ||
  //   ||
  //   ||
  //   ||
  //   ||
  //   ||
  //   ||
  //   ||
  //   ||
  //   ||
  //   ||
  //   ||
  //   ||
  //   ||
  //   ||
  //   ||
  //   ||
  //   ||
  //   ||
  //   ||
  //   ||
  //   ||
  //   ||
  //   ||
  //   ||
  //   ||
  //   ||
  //   ||
  //   ||
  //   ||
  //   ||
  //   ||
  //   ||
  //   ||
  //   ||
  //   ||
  //   ||
  //   ||
  //   ||
  //   ||
  //   ||
  //   ||
  //   ||
  //   ||
  //   ||
  //   ||
  //   ||
  //   ||
  //   ||
  //   ||
  //   ||
  //   ||
  //   ||
  //   ||
  //   ||
  //   ||
  //   ||
  //   ||
  //   ||
  //   ||
  //   ||
  //   ||
  //   ||
  //   ||
  //   ||
  //   ||
  //   ||
  //   ||
  //   ||
  //   ||
  //   ||
  //   ||
  //   ||
  //   ||
  //   ||
  //   ||
  //   ||
  //   ||
  //   ||
  //   ||
  //   ||
  //   ||
  //   ||
  //   ||
  //   ||
  //   ||
  //   ||
  //   ||
  //   ||
  //   ||
  //   ||
  //   ||
  //   ||
  //   ||
  //   ||
  //   ||
  //   ||
  //   ||
  //   ||
  //   ||
  //   ||
  //   ||
  //   ||
  //   ||
  //   ||
  //   ||
  //   ||
  //   ||
  //   ||
  //   ||
  //   ||
  //   ||
  //   ||
  //   ||
  //   ||
  //   ||
  //   ||
  //   ||
  //   ||
  //   ||
  //   ||
  //   ||
  //   ||
  //   ||
  //   ||
  //   ||
  //   ||
  //   ||
  //   ||
  //   ||
  //   =====================================================
  //   Updating Tag depending on the block turned on
  //   =====================================================
  //   Ckecking the current CPU tag for a Match
  //   ||
  //   ||
  //   ||
  //   ||
  //   ||
  //   ||
  //   ||
  //   ||
  //   ||
  //   ||
  //   ||
  //   ||
  //   ||
  //   ||
  //   ||
  //   ||
  //   ||
  //   ||
  //   ||
  //   ||
  //   ||
  //   ||
  //   ||
  //   ||
  //   ||
  //   ||
  //   ||
  //   ||
  //   ||
  //   ||
  //   ||
  //   ||
  //   ||
  //   ||
  //   ||
  //   ||
  //   ||
  //   ||
  //   ||
  //   ||
  //   ||
  //   ||
  //   ||
  //   ||
  //   ||
  //   ||
  //   ||
  //   ||
  //   ||
  //   ||
  //   ||
  //   ||
  //   ||
  //   ||
  //   ||
  //   ||
  //   ||
  //   ||
  //   ||
  //   ||
  //   ||
  //   ||
  //   ||
  //   ||
  //   ||
  //   ||
  //   ||
  //   ||
  //   ||
  //   ||
  //   ||
  //   ||
  //   ||
  //   ||
  //   ||
  //   ||
  //   ||
  //   ||
  //   ||
  //   ||
  //   ||
  //   ||
  //   ||
  //   ||
  //   ||
  //   ||
  //   ||
  //   ||
  //   ||
  //   ||
  //   ||
  //   ||
  //   ||
  //   ||
  //   ||
  //   ||
  //   ||
  //   ||
  //   ||
  //   ||
  //   ||
  //   ||
  //   ||
  //   ||
  //   ||
  //   ||
  //   ||
  //   ||
  //   ||
  //   ||
  //   ||
  //   ||
  //   ||
  //   ||
  //   ||
  //   ||
  //   ||
  //   ||
  //   ||
  //   ||
  //   ||
  //   ||
  //   ||
  //   ||
  //   ||
  //   ||
  //   ||
  //   ||
  //   ||
  //   ||
  //   ||
  //   ||
  //   ||
  //   ||
  //   ||
  //   ||
  //   ||
  //   ||
  //   ||
  //   ||
  //   ||
  //   ||
  //   ||
  //   ||
  //   ||
  //   ||
  //   ||
  //   ||
  //   ||
  //   ||
  //   ||
  //   ||
  //   ||
  //   ||
  //   ||
  //   ||
  //   ||
  //   ||
  //   ||
  //   ||
  //   ||
  //   ||
  //   ||
  //   ||
  //   ||
  //   ||
  //   ||
  //   ||
  //   ||
  //   ||
  //   ||
  //   ||
  //   ||
  //   ||
  //   ||
  //   ||
  //   ||
  //   ||
  //   ||
  //   ||
  //   ||
  //   ||
  //   ||
  //   ||
  //   ||
  //   ||
  //   ||
  //   ||
  //   ||
  //   ||
  //   ||
  //   ||
  //   ||
  //   ||
  //   ||
  //   ||
  //   ||
  //   ||
  //   ||
  //   ||
  //   ||
  //   ||
  //   ||
  //   ||
  //   ||
  //   ||
  //   ||
  //   ||
  //   ||
  //   ||
  //   ||
  //   ||
  //   ||
  //   ||
  //   ||
  //   ||
  //   ||
  //   ||
  //   ||
  //   ||
  //   2
  //   (The address to memory that your cache would like to read from or write to.)
  //   set equal to the addres I WANT TO READ OR WRITE TO
  //   (The value of the byte at CpuAddress when the CPU makes a read request. )
endmodule

module Kick_Out_the_Oldest_Age_Only (
  input  Contain,
  input  [2:0] Counter,
  input  [1:0] Age_at__00__Saved,
  input  [1:0] Age_at__01__Saved,
  input  [1:0] Age_at__10__Saved,
  output Kick_Out_Age_In_Block_1,
  output Kick_Out_Age_In_Block_2,
  output Kick_Out_Age_In_Block_3
);

  wire comparator_3_gt, comparator_4_eq, comparator_5_eq, comparator_6_gt, comparator_7_gt, comparator_8_eq,
       Kick_Out_Enabled;
  wire [1:0] adder_1_out, adder_2_out, adder_3_out;

  Shift_Register #(.length(5)) Dividend ();  // open: shift, in, clk, out, load, clr, d0, q0, d1, q1, d2, q2, d3, q3, d4, q4
  Register #(.width(5)) register_1 ();  // open: D, en, Q, clk, clr
  Comparator #(.width(5), .mode("unsigned")) comparator_1 ();  // open: a, b, gt, eq, lt
  Multiplexer #(.width(5), .enable("false")) multiplexer_1 ();  // open: in0, in1, out, sel
  Shifter #(.width(5)) shifter_1 ();  // open: in, dist, out
  Bit_Extender #(.in_width(1), .out_width(5), .\type ("sign")) bit_extender_1 ();  // open: in, out
  Subtractor #(.width(5)) subtractor_1 ();  // open: a, b, out, bin, bout
  Counter #(.width(3), .max('h6)) Bits_Left ();  // open: load, D, count, Q, carry, clk, clr
  Comparator #(.width(3), .mode("unsigned")) comparator_2 (
    .a(Counter), .b(3'b010), .eq(Kick_Out_Enabled));  // open: gt, lt
  // Probe on 3'b010
  Adder #(.width(2)) adder_1 (.a(Age_at__01__Saved), .b(Age_at__10__Saved), .out(adder_1_out));  // open: cin, cout
  Adder #(.width(2)) adder_2 (.a(Age_at__00__Saved), .b(Age_at__10__Saved), .out(adder_2_out));  // open: cin, cout
  // Probe on Age_at__00__Saved
  Comparator #(.width(2), .mode("unsigned")) comparator_3 (
    .a(Age_at__00__Saved), .b(adder_1_out), .gt(comparator_3_gt));  // open: eq, lt
  // Probe on adder_1_out
  // Probe on Age_at__01__Saved
  // Probe on adder_2_out
  Comparator #(.width(1), .mode("unsigned")) comparator_4 (
    .a(Kick_Out_Enabled), .b(1'b1), .eq(comparator_4_eq));  // open: gt, lt
  Comparator #(.width(1), .mode("unsigned")) comparator_5 (
    .a(Kick_Out_Enabled), .b(1'b1), .eq(comparator_5_eq));  // open: gt, lt
  Comparator #(.width(2), .mode("unsigned")) comparator_6 (
    .a(Age_at__01__Saved), .b(adder_2_out), .gt(comparator_6_gt));  // open: eq, lt
  and and_1 (Kick_Out_Age_In_Block_1, comparator_4_eq, comparator_3_gt);
  and and_2 (Kick_Out_Age_In_Block_2, comparator_5_eq, comparator_6_gt);
  // Probe on Age_at__10__Saved
  Adder #(.width(2)) adder_3 (.a(Age_at__00__Saved), .b(Age_at__01__Saved), .out(adder_3_out));  // open: cin, cout
  // Probe on adder_3_out
  Comparator #(.width(2), .mode("unsigned")) comparator_7 (
    .a(Age_at__10__Saved), .b(adder_3_out), .gt(comparator_7_gt));  // open: eq, lt
  Comparator #(.width(1), .mode("unsigned")) comparator_8 (
    .a(Kick_Out_Enabled), .b(1'b1), .eq(comparator_8_eq));  // open: gt, lt
  and and_3 (Kick_Out_Age_In_Block_3, comparator_8_eq, comparator_7_gt);

  // Other names for the same wires on the sheet: Age_00_at_Block_1[1:0] = Age_at__00__Saved;
  //   Age_01_at_Block_2[1:0] = Age_at__01__Saved; Age_10_at_Block_3[1:0] = Age_at__10__Saved
endmodule

module My_Block (
  input  Set,
  input  [6:0] Final_TAG,
  input  [6:0] CpuAddress_Saved,
  input  Dirty,
  input  Valid,
  input  [1:0] Age,
  input  [7:0] Value_00,
  input  [7:0] Value_01,
  input  [7:0] Value_10,
  input  [7:0] Value_11,
  input  CLK,
  output Updated_Dirty,
  output Updated_Valid,
  output [1:0] Updated_Age,
  output [7:0] Value_00_Updated,
  output [7:0] Value_01_Updated,
  output [7:0] Value_10_Updated,
  output [7:0] Value_11_Updated
);

  Shift_Register #(.length(5)) Dividend ();  // open: shift, in, clk, out, load, clr, d0, q0, d1, q1, d2, q2, d3, q3, d4, q4
  Register #(.width(5)) register_1 ();  // open: D, en, Q, clk, clr
  Comparator #(.width(5), .mode("unsigned")) comparator_1 ();  // open: a, b, gt, eq, lt
  Multiplexer #(.width(5), .enable("false")) multiplexer_1 ();  // open: in0, in1, out, sel
  Shifter #(.width(5)) shifter_1 ();  // open: in, dist, out
  Bit_Extender #(.in_width(1), .out_width(5), .\type ("sign")) bit_extender_1 ();  // open: in, out
  Subtractor #(.width(5)) subtractor_1 ();  // open: a, b, out, bin, bout
  Adder #(.width(2)) adder_1 ();  // open: a, b, out, cin, cout
  Counter #(.width(3), .max('h6)) Bits_Left ();  // open: load, D, count, Q, carry, clk, clr
  // Probe on Dirty
  // Probe on Valid
  // Probe on Age
  // Probe on Updated_Dirty
  Register #(.width(1)) register_2 (.D(Dirty), .en(Set), .Q(Updated_Dirty), .clk(CLK));  // open: clr
  // Probe on Updated_Valid
  Register #(.width(1)) register_3 (.D(Valid), .en(Set), .Q(Updated_Valid), .clk(CLK));  // open: clr
  // Probe on Updated_Age
  Register #(.width(2)) register_4 (.D(Age), .en(Set), .Q(Updated_Age), .clk(CLK));  // open: clr
  Register #(.width(7)) register_5 (.D(CpuAddress_Saved), .en(Set), .Q(Final_TAG), .clk(CLK));  // open: clr
  Register register_6 (.D(Value_00), .en(Set), .Q(Value_00_Updated), .clk(CLK));  // open: clr
  Register register_7 (.D(Value_01), .en(Set), .Q(Value_01_Updated), .clk(CLK));  // open: clr
  Register register_8 (.D(Value_10), .en(Set), .Q(Value_10_Updated), .clk(CLK));  // open: clr
  Register register_9 (.D(Value_11), .en(Set), .Q(Value_11_Updated), .clk(CLK));  // open: clr

  // Other names for the same wires on the sheet: Kick_out_Age___replace_inthisBlock = Set;
  //   Most_Recent_Updated_Age_Is[1:0] = Updated_Age; Most_Recent_Updated_Dirty_Is = Updated_Dirty;
  //   Most_Recent_Updated_Valid_Is = Updated_Valid; MostRecent_Updated_Tag_Is[6:0] = Final_TAG; My_Age_Is[1:0] = Age;
  //   My_Dirty_Is = Dirty; My_Valid_Is = Valid; Tag_InthisBlock_Saved[6:0] = CpuAddress_Saved;
  //   Value_00_Going_In[7:0] = Value_00; Value_01_Going_In[7:0] = Value_01; Value_10_Going_In[7:0] = Value_10;
  //   Value_11_Going_In[7:0] = Value_11

  // Notes on the sheet:
  //   Saving The Dirty that comes in this Block
endmodule
