// Logisim project Vending-Machine.circ as structural Verilog: 6 circuits, main circuit main
module main (
  input  Halt_Enable
);

  wire and_2_out, CLK, Correct, Dime, Done_Testing, Give_Dime, Give_Merch, Give_Nickel, Halt, Nickel,
       not_1_out, not_2_out, not_3_out, Quarter, Sol_Give_Dime, Sol_Give_Merch, Sol_Give_Nickel;
  wire [8:0] counter_1_q, TestNumber;

  Clock clock_1 (.out(CLK));
  not not_1 (not_1_out, Correct);
  and and_1 (Halt, Halt_Enable, not_1_out);
  Inputs inputs_1 (
    .Halt(Halt), .CLK(CLK), .Quarter(Quarter), .Dime(Dime), .Nickel(Nickel), .TestNumber(TestNumber),
    .Done_Testing(Done_Testing));
  // Probe on Quarter
  // Probe on Dime
  // Probe on Nickel
  Vending vending_1 (
    .Quarter(Quarter), .Dime(Dime), .Nickel(Nickel), .CLK(CLK), .Give_Merchandise(Give_Merch),
    .Give_Dime(Give_Dime), .Give_Nickel(Give_Nickel));
  // Probe on Correct
  // Probe on Give_Merch
  // Probe on Sol_Give_Merch
  // Probe on Give_Dime
  // Probe on Sol_Give_Dime
  // Probe on Give_Nickel
  // Probe on Sol_Give_Nickel
  not not_2 (not_2_out, Halt);
  Checker checker_1 (
    .Give_Merch(Give_Merch), .Give_Dime(Give_Dime), .Give_Nickel(Give_Nickel), .TestNumber(TestNumber),
    .Correct(Correct), .Sol_Give_Merch(Sol_Give_Merch), .Sol_Give_Dime(Sol_Give_Dime),
    .Sol_Give_Nickel(Sol_Give_Nickel));
  and and_2 (and_2_out, Correct, not_2_out, not_3_out);
  not not_3 (not_3_out, Done_Testing);
  // Probe on counter_1_q
  Counter #(.width(9), .max('h162), .ongoal("stay")) counter_1 (
    .count(and_2_out), .Q(counter_1_q), .clk(CLK));  // open: load, D, carry, clr

  // Notes on the sheet:
  //   Max 354
  //   Brayan Vera, 913058288 
  //   Nhi Vo, 912796677
endmodule

module Vending (
  input  Quarter,
  input  Dime,
  input  Nickel,
  input  CLK,
  output Give_Merchandise,
  output Give_Dime,
  output Give_Nickel
);

  wire [2:0] next_state_vending_1_b0p, register_1_q;

  Next_State_Vending next_state_vending_1 (
    .B2(register_1_q[2]), .B1(register_1_q[1]), .B0(register_1_q[0]), .Q(Quarter), .D(Dime), .N(Nickel),
    .B2P(next_state_vending_1_b0p[2]), .B1P(next_state_vending_1_b0p[1]), .B0P(next_state_vending_1_b0p[0]));
  Register #(.width(3)) register_1 (.D(next_state_vending_1_b0p), .Q(register_1_q), .clk(CLK));  // open: en, clr
  Output output_1 (
    .X1(register_1_q[2]), .X2(register_1_q[1]), .X3(register_1_q[0]), .Q(Quarter), .D(Dime), .N(Nickel),
    .Z1(Give_Merchandise), .Z2(Give_Dime), .Z3(Give_Nickel));

  // Other names for the same wires on the sheet: GD = Give_Dime; GM = Give_Merchandise; GN = Give_Nickel;
  //   Quater = Quarter
endmodule

module Inputs (
  input  Halt,
  input  CLK,
  output Quarter,
  output Dime,
  output Nickel,
  output [8:0] TestNumber,
  output Done_Testing
);

  wire not_1_out;

  not not_1 (not_1_out, Halt);
  Counter #(.width(9), .max('h162), .ongoal("stay")) counter_1 (
    .count(not_1_out), .Q(TestNumber), .carry(Done_Testing), .clk(CLK));  // open: load, D, clr
  ROM #(.addrWidth(9), .dataWidth(3)) rom_1 (.addr(TestNumber), .data({Quarter, Dime, Nickel}));  // open: sel

  // Notes on the sheet:
  //   contents of rom_1 (hex, n*v repeats v):
  //   1 0 1 0 1 0 1 0 1 0 1 0 1 0 1 0 1 0 1 0 1 0 2 0 1 0 1 0 1 0 1 0 1 0 4 0 1 0 1 0 1 0 1 0 2 0 1 0 1 0
  //   1 0 1 0 4 0 1 0 1 0 1 0 1 0 2 0 1 0 1 0 1 0 2 0 2 0 1 0 1 0 1 0 2 0 4 0 1 0 1 0 1 0 4 0 1 0 1 0 1 0
  //   1 0 2 0 1 0 1 0 1 0 2 0 2 0 1 0 1 0 1 0 2 0 4 0 1 0 1 0 2 0 2 0 1 0 1 0 2 0 4 0 1 0 1 0 4 0 1 0 1 0
  //   1 0 1 0 2 0 1 0 1 0 1 0 2 0 2 0 1 0 1 0 1 0 2 0 4 0 1 0 1 0 2 0 2 0 1 0 1 0 2 0 4 0 1 0 1 0 2 0 2 0
  //   1 0 2 0 2 0 2 0 1 0 2 0 2 0 4 0 1 0 2 0 4 0 1 0 4 0 1 0 1 0 1 0 1 0 2 0 1 0 1 0 1 0 2 0 2 0 1 0 1 0
  //   1 0 2 0 4 0 1 0 1 0 2 0 2 0 1 0 1 0 2 0 4 0 1 0 1 0 2 0 2 0 1 0 2 0 2 0 2 0 1 0 2 0 2 0 4 0 1 0 2 0
  //   4 0 1 0 1 0 2 0 2 0 1 0 2 0 2 0 2 0 1 0 2 0 2 0 4 0 2 0 2 0 2 0 2 0 2 0 4 0 2 0 4 0 1 0 4 0 2 0 4 0
  //   4 0 4
endmodule

module Checker (
  input  Give_Merch,
  input  Give_Dime,
  input  Give_Nickel,
  input  [8:0] TestNumber,
  output Correct,
  output Sol_Give_Merch,
  output Sol_Give_Dime,
  output Sol_Give_Nickel
);

  ROM #(.addrWidth(9), .dataWidth(3)) rom_1 (
    .addr(TestNumber), .data({Sol_Give_Merch, Sol_Give_Dime, Sol_Give_Nickel}));  // open: sel
  Comparator #(.width(3)) comparator_1 (
    .a({Sol_Give_Merch, Sol_Give_Dime, Sol_Give_Nickel}), .b({Give_Merch, Give_Dime, Give_Nickel}),
    .eq(Correct));  // open: gt, lt

  // Other names for the same wires on the sheet: Solution[2:0] = {Sol_Give_Merch, Sol_Give_Dime, Sol_Give_Nickel};
  //   Your_Answer[2:0] = {Give_Merch, Give_Dime, Give_Nickel}

  // Notes on the sheet:
  //   contents of rom_1 (hex, n*v repeats v):
  //   10*0 4 11*0 5 11*0 7 9*0 4 9*0 7 9*0 4 9*0 5 9*0 7 7*0 6 9*0 4 9*0 5 9*0 7 7*0 4 7*0 7 5*0 5 9*0 4
  //   9*0 5 9*0 7 7*0 4 7*0 7 7*0 4 7*0 5 7*0 7 5*0 6 0 0 0 4 9*0 4 9*0 5 9*0 7 7*0 4 7*0 7 7*0 4 7*0 5
  //   7*0 7 5*0 6 7*0 4 7*0 5 7*0 7 5*0 4 5*0 7 0 0 0 5 0 0 0 4 0 0 0 5 0 0 0 7
endmodule

module Next_State_Vending (
  input  B2,
  input  B1,
  input  B0,
  input  Q,
  input  D,
  input  N,
  output B2P,
  output B1P,
  output B0P
);

  wire and_1_out, and_2_out, and_3_out, and_4_out, and_5_out, and_6_out, and_7_out, and_8_out, and_9_out,
       and_10_out, and_11_out, and_12_out, and_13_out, and_14_out, and_15_out, and_16_out, and_17_out,
       and_18_out, not_1_out, not_2_out, not_3_out, not_4_out, not_5_out, not_6_out, not_7_out, not_8_out,
       not_9_out, not_10_out, not_11_out, not_12_out, not_13_out, not_14_out, not_15_out, not_16_out,
       not_17_out, not_18_out, not_19_out, not_20_out, not_21_out, not_22_out, not_23_out, not_24_out,
       not_25_out, not_26_out, not_27_out, not_28_out, not_29_out, not_30_out, not_31_out, not_32_out,
       not_33_out, not_34_out, not_35_out, not_36_out, not_37_out, not_38_out, not_39_out, not_40_out,
       not_41_out, not_42_out, not_43_out, not_44_out, not_45_out, not_46_out, not_47_out, not_48_out;

  not not_1 (not_1_out, B2);
  not not_2 (not_2_out, B1);
  not not_3 (not_3_out, B0);
  not not_4 (not_4_out, D);
  not not_5 (not_5_out, N);
  not not_6 (not_6_out, Q);
  not not_7 (not_7_out, B0);
  not not_8 (not_8_out, Q);
  not not_9 (not_9_out, D);
  not not_10 (not_10_out, B2);
  not not_11 (not_11_out, Q);
  not not_12 (not_12_out, N);
  not not_13 (not_13_out, B0);
  not not_14 (not_14_out, Q);
  not not_15 (not_15_out, D);
  not not_16 (not_16_out, N);
  not not_17 (not_17_out, B1);
  not not_18 (not_18_out, D);
  not not_19 (not_19_out, N);
  not not_20 (not_20_out, B2);
  not not_21 (not_21_out, B1);
  not not_22 (not_22_out, Q);
  not not_23 (not_23_out, B1);
  not not_24 (not_24_out, Q);
  not not_25 (not_25_out, Q);
  not not_26 (not_26_out, D);
  not not_27 (not_27_out, B2);
  not not_28 (not_28_out, Q);
  not not_29 (not_29_out, D);
  not not_30 (not_30_out, Q);
  not not_31 (not_31_out, D);
  not not_32 (not_32_out, N);
  not not_33 (not_33_out, Q);
  not not_34 (not_34_out, N);
  not not_35 (not_35_out, B2);
  not not_36 (not_36_out, B1);
  not not_37 (not_37_out, Q);
  not not_38 (not_38_out, D);
  not not_39 (not_39_out, B2);
  not not_40 (not_40_out, B1);
  not not_41 (not_41_out, B0);
  not not_42 (not_42_out, Q);
  not not_43 (not_43_out, N);
  not not_44 (not_44_out, Q);
  not not_45 (not_45_out, D);
  not not_46 (not_46_out, N);
  not not_47 (not_47_out, B1);
  not not_48 (not_48_out, Q);
  and and_1 (and_1_out, not_1_out, not_2_out, not_3_out, Q, not_4_out, not_5_out);
  and and_2 (and_2_out, B0, not_6_out, D, N);
  and and_3 (and_3_out, B1, not_7_out, not_8_out, not_9_out, N);
  and and_4 (and_4_out, not_10_out, B1, not_11_out, D, not_12_out);
  and and_5 (and_5_out, B1, not_13_out, Q, D, N);
  and and_6 (and_6_out, B2, not_14_out, not_15_out, not_16_out);
  and and_7 (and_7_out, B2, not_17_out, Q, not_18_out, N);
  and and_8 (and_8_out, B2, Q, D, not_19_out);
  and and_9 (and_9_out, not_20_out, not_21_out, not_22_out, D);
  and and_10 (and_10_out, not_23_out, not_24_out, D, N);
  and and_11 (and_11_out, B0, not_25_out, not_26_out, N);
  and and_12 (and_12_out, not_27_out, B1, not_28_out, not_29_out);
  and and_13 (and_13_out, B1, not_30_out, not_31_out, not_32_out);
  and and_14 (and_14_out, B1, B0, not_33_out, not_34_out);
  and and_15 (and_15_out, not_35_out, not_36_out, not_37_out, not_38_out, N);
  and and_16 (and_16_out, not_39_out, not_40_out, not_41_out, not_42_out, D, not_43_out);
  and and_17 (and_17_out, B0, not_44_out, not_45_out, not_46_out);
  and and_18 (and_18_out, B2, not_47_out, not_48_out, D, N);
  or or_1 (B2P, and_1_out, and_2_out, and_3_out, and_4_out, and_5_out, and_6_out, and_7_out, and_8_out);
  or or_2 (B1P, and_9_out, and_10_out, and_11_out, and_12_out, and_13_out, and_14_out);
  or or_3 (B0P, and_15_out, and_16_out, and_17_out, and_18_out);
endmodule

module Output (
  input  X1,
  input  X2,
  input  X3,
  input  Q,
  input  D,
  input  N,
  output Z1,
  output Z2,
  output Z3
);

  wire and_1_out, and_2_out, and_3_out, and_4_out, and_5_out, and_6_out, and_7_out, and_8_out, and_9_out,
       and_10_out, and_11_out, and_12_out, and_13_out, and_14_out, and_15_out, and_16_out, and_17_out,
       and_18_out, and_19_out, and_20_out, and_21_out, and_22_out, not_1_out, not_2_out, not_3_out,
       not_4_out, not_5_out, not_6_out, not_7_out, not_8_out, not_9_out, not_10_out, not_11_out;

  not not_1 (not_1_out, X3);
  not not_2 (not_2_out, X2);
  not not_3 (not_3_out, X3);
  not not_4 (not_4_out, X2);
  not not_5 (not_5_out, X3);
  not not_6 (not_6_out, N);
  not not_7 (not_7_out, X2);
  not not_8 (not_8_out, X3);
  not not_9 (not_9_out, N);
  not not_10 (not_10_out, X2);
  not not_11 (not_11_out, N);
  and and_1 (and_1_out, Q, N);
  and and_2 (and_2_out, Q, D);
  and and_3 (and_3_out, X3, Q);
  and and_4 (and_4_out, X2, not_1_out, D, N);
  and and_5 (and_5_out, X2, Q);
  and and_6 (and_6_out, X1, not_2_out, N);
  and and_7 (and_7_out, X1, D);
  and and_8 (and_8_out, X1, Q);
  and and_9 (and_9_out, Q, D, N);
  and and_10 (and_10_out, X3, Q, D);
  and and_11 (and_11_out, X2, not_3_out, Q);
  and and_12 (and_12_out, X2, Q, N);
  and and_13 (and_13_out, X1, not_4_out, D, N);
  and and_14 (and_14_out, X1, Q);
  and and_15 (and_15_out, not_5_out, Q, D, not_6_out);
  and and_16 (and_16_out, not_7_out, X3, Q, N);
  and and_17 (and_17_out, X2, not_8_out, Q, N);
  and and_18 (and_18_out, X2, Q, D);
  and and_19 (and_19_out, X2, X3, Q, not_9_out);
  and and_20 (and_20_out, X1, not_10_out, D, not_11_out);
  and and_21 (and_21_out, X1, Q);
  and and_22 (and_22_out, X1, X2, D, N);
  or or_1 (Z1, and_1_out, and_2_out, and_3_out, and_4_out, and_5_out, and_6_out, and_7_out, and_8_out);
  or or_2 (Z2, and_9_out, and_10_out, and_11_out, and_12_out, and_13_out, and_14_out);
  or or_3 (Z3, and_15_out, and_16_out, and_17_out, and_18_out, and_19_out, and_20_out, and_21_out, and_22_out);
endmodule
